# Fritzing sketch ArduinoNano (saved by Fritzing 0.9.4)
breadboards: 1

parts:
  Componente1 = Arduino Nano (Rev3.0)
  SEN1 = Pulse Sensor [package=SIP-3]
  Componente2 = FC-03 [chip_label=FC-03]
  Componente3 = LCD1602-I2C
  M1 = fc-51 [package=THT]
  hc-sr1 = hc-sr04
  J1 = Piezo Speaker
  LED1 = LEDs [package=led10mm]
  R1 = Resistor [tolerance=±5% resistance=220 package=THT]
  U1 = ESP8266 NodeMCU LoLin module

nets:
  GND: Componente1.GND, SEN1.GND, Componente2.pin_2, Componente3.GND, M1.pin1, hc-sr1.GND, J1.pin1, LED1.A, U1.GND
  N1: Componente1.D4, hc-sr1.Trig
  N2: Componente1.D5, hc-sr1.Echo
  N3: Componente1.D7, J1.pin2
  N4: Componente1.D10, U1.TX
  N5: Componente1.D11/MOSI, U1.RX
  N6: Componente1.D12/MISO, R1.Pin_0
  VCC: Componente1.5V, Componente3.VCC, M1.pin3, hc-sr1.VCC
  N7: Componente1.A5, Componente3.SCL
  N8: Componente1.A4, Componente3.SDA
  N9: Componente1.A1, M1.pin2
  N10: Componente1.A0, SEN1.Signal
  3V3: Componente1.3V3, SEN1.VCC, Componente2.pin_1
  N11: Componente1.D13/SCK, Componente2.pin_3
  N12: LED1.C, R1.Pin_1

custom parts:
  Pulse Sensor: Pulse Sensor Optical Heart Beat Sensor
  FC-03: FC-03, LM393 IR Speed Sensor Encoder
  LCD1602-I2C: A standard character display, usually with 2x16 characters. Comes in many colors with LCM1602 IIC attached.
  ESP8266 NodeMCU LoLin module: ESP8266 based NodeMCU
